# Fritzing sketch shema-petit-bot-2alim (saved by Fritzing 0.9.3b)

parts:
  WeMos_D1_Mini1 = WeMos D1 Mini
  M1 = Dagu DGServo 9g (Top view) [part_number=RS001B]
  BATT1 = 4xAA Switchable Battery Pack w/JST connector
  VCC1 = Battery
  M2 = Dagu DGServo 9g (Top view) [part_number=RS001B]
  S1 = Taiway 100-SP-X-T1 SPDT Miniature Toggle Switch [part_number=100-SP-X-T1-0-0-B1-M1 package=THT]

nets:
  N1: WeMos_D1_Mini1.3V3, S1.L2
  N2: WeMos_D1_Mini1.D2, M2.pulse
  N3: WeMos_D1_Mini1.D3, M1.pulse
  GND: WeMos_D1_Mini1.G, M1.gnd, BATT1.NEG, VCC1.-, M2.gnd
  VCC: M1.vcc, BATT1.POS, M2.vcc
  N4: VCC1.+, S1.COM

custom parts:
  4xAA Switchable Battery Pack w/JST connector: 4xAA Switchable Battery Pack with JST connector
