# Fritzing sketch shema-petit-bot-decompose-controles (saved by Fritzing 0.9.3b)

parts:
  M1 = Dagu DGServo 9g (Top view) [part_number=RS001B]
  M2 = Dagu DGServo 9g (Top view) [part_number=RS001B]
  WeMos_D1_Mini3 = WeMos D1 Mini

nets:
  N1: M1.pulse, WeMos_D1_Mini3.D2
  N2: M2.pulse, WeMos_D1_Mini3.D1
