# Fritzing sketch shema-petit-bot-battery5V (saved by Fritzing 0.9.3b)

parts:
  Composant2 = Lithium Ion Polymer Battery 3.7v 2500mAh [part_number=328]
  WeMos_D1_Mini1 = WeMos D1 Mini
  M1 = Dagu DGServo 9g (Top view) [part_number=RS001B]
  M2 = Dagu DGServo 9g (Top view) [part_number=RS001B]
  S1 = Taiway 100-SP-X-T1 SPDT Miniature Toggle Switch [part_number=100-SP-X-T1-0-0-B1-M1 package=THT]

nets:
  N1: Composant2.positive, S1.COM
  GND: Composant2.negative, WeMos_D1_Mini1.G, M1.gnd, M2.gnd
  VCC: WeMos_D1_Mini1.5V, M1.vcc, M2.vcc, S1.L1
  N2: WeMos_D1_Mini1.D1, M1.pulse
  N3: WeMos_D1_Mini1.D2, M2.pulse

custom parts:
  Lithium Ion Polymer Battery 3.7v 2500mAh: Lithium ion polymer (also known as 'lipo' or 'lipoly') batteries are thin, light and powerful. The output ranges from 4.2V when completely charged to 3.7V. This battery has a capacity of 2500mAh for a total of about 10 Wh. The batteries come pre-attached with a genuine 2-pin JST-PH connector as shown and include the necessary protection circuitry.
