# Fritzing sketch shema-petit-bot (saved by Fritzing 0.9.3b)

parts:
  M1 = Dagu DGServo 9g (Top view) [part_number=RS001B]
  M2 = Dagu DGServo 9g (Top view) [part_number=RS001B]
  BATT1 = 3xAAA Switchable Battery Pack w/Bare Wire
  WeMos_D1_Mini3 = WeMos D1 Mini

nets:
  GND: M1.gnd, M2.gnd, BATT1.NEG, WeMos_D1_Mini3.G
  VCC: M1.vcc, M2.vcc, BATT1.POS, WeMos_D1_Mini3.5V
  N1: M1.pulse, WeMos_D1_Mini3.D2
  N2: M2.pulse, WeMos_D1_Mini3.D1

custom parts:
  3xAAA Switchable Battery Pack w/Bare Wire: 3xAAA Switchable Battery Pack w/Bare Wire Connectors
